# Fritzing sketch neuron_arduino_connections_1 (saved by Fritzing 0.9.3b)

parts:
  Part3 = Arduino Leonardo (Rev3b)
  R1 = Slide Potentiometer [maximum_resistance=100kΩ]
  S1 = Round Pushbutton
  R2 = Slide Potentiometer [maximum_resistance=100kΩ]

nets:
  N1: Part3.5V, R1.leg2, R2.leg2
  N2: Part3.GND, R1.leg1, S1.leg1, R2.leg1
  N3: Part3.A0, R2.wiper
  N4: Part3.A1, R1.wiper
  N5: Part3.A2, S1.leg0
